# Fritzing sketch AutomatedIrrigatingSystem (saved by Fritzing 0.9.3b)
breadboards: 1

parts:
  Part1 = Arduino Mega 2560 (Rev3)
  U1 = ESP8266 WiFi Module [part_number=ESP8266]
  R1 = Resistor [tolerance=±5% resistance=10k package=THT]
  R2 = Resistor [tolerance=±5% resistance=10k package=THT]
  S1 = Temperature Sensor (Thermistor) [thermistor_type=NTC package=THT]
  R4 = Resistor [tolerance=±5% resistance=10k package="0805 [SMD]"]
  U2 = RELAY [package=relay-jzc]
  U3 = RELAY [package=relay-jzc]
  U4 = RELAY [package=relay-jzc]
  U5 = RELAY [package=relay-jzc]
  U9_3_3V = LMZ14203 [package=to-pmod-7]
  U10_5V = LMZ14203 [package=to-pmod-7]
  R5 = Resistor [tolerance=±5% resistance=0 package="1206 [SMD]"]
  M1 = DC Motor
  L1 = Solenoid
  L2 = Solenoid
  L3 = Solenoid
  D1 = Rectifier Diode [part_number=1N4001 package="300 mil [THT]"]
  D2 = Rectifier Diode [part_number=1N4001 package="300 mil [THT]"]
  D3 = Rectifier Diode [part_number=1N4001 package="300 mil [THT]"]
  D4 = Rectifier Diode [part_number=1N4001 package="300 mil [THT]"]
  Power_plug1 = Power plug
  R6 = Resistor [tolerance=±5% resistance=10k package=THT]
  R7 = Resistor [tolerance=±5% resistance=10k package=THT]
  R8 = Resistor [tolerance=±5% resistance=22k package=THT]
  R9 = Resistor [tolerance=±5% resistance=22k package=THT]
  R10 = Resistor [tolerance=±5% resistance=10k package=THT]
  R11 = Resistor [tolerance=±5% resistance=22k package=THT]

nets:
  N1: Part1.A0, S1.pin_0, R4.Pin_0
  N2: Part1.D19/RX1, R6.Pin_1
  N3: Part1.D18/TX1, R7.Pin_1
  N4: Part1.D9_PWM, R10.Pin_1
  N5: Part1.D8_PWM, U2.MAIN
  GND: Part1.GND, U1.GND, R1.Pin_1, R2.Pin_1, R4.Pin_1, R5.Pin_0, R8.Pin_0, R9.Pin_0, R11.Pin_0
  N6: Part1.VIN, S1.pin_1, U5.MAIN, U10_5V.EP
  N7: Part1.D3_PWM, R1.Pin_0
  N8: Part1.D4_PWM, R2.Pin_0
  N9: Part1.D5_PWM, U4.MAIN
  N10: Part1.D6_PWM, U4.COIL1
  N11: Part1.D7_PWM, U3.MAIN
  N12: U1.RST, R10.Pin_0
  N13: U1.TX, R8.Pin_1
  N14: U1.RX, R9.Pin_1
  N15: U1.3.3V, U9_3_3V.EP
  N16: U2.COIL2, D2.cathode
  GND_2: U2.NC, U3.NC, U4.NC, U5.NC, U9_3_3V.GND, U10_5V.GND, Power_plug1.GND
  N17: U3.COIL2, D1.cathode
  N18: U4.COIL2, L2.pin2
  N19: U5.COIL2, D4.cathode
  N20: U5.COIL1, U9_3_3V.VOUT, U10_5V.VOUT, R5.Pin_1
  VIN: U9_3_3V.VIN, U10_5V.VIN, M1.pin_1, L1.pin1, L2.pin1, L3.pin1, D1.anode, D2.anode, D3.anode, D4.anode, Power_plug1.VCC

notes:
  3 pins :
  + green: power out
  + grey: input prealert
  +white: input alert
  -These are used to check water level periodically
  - 1 means there is water at that level
  -0 means no water at that level.
  Replace R5 later with 10k and check for voltage drop to see if there are differences between ground.
  pump-solenoid3-solenoid2-solenoid1
  NO and base
  12V 2A power supply
  To add :
  + water volumn counter
